# Fritzing sketch 1-LCD (saved by Fritzing 0.9.3b)
breadboards: 1

parts:
  Arduino = Arduino Uno (Rev3)
  Pantalla_LCD = LCD screen
  Potenciómetro = TRIMPOT [package=trimpot_pth_s3_lock]

nets:
  N1: Arduino.D11_PWM/MOSI, Pantalla_LCD.E
  N2: Arduino.D12/MISO, Pantalla_LCD.RS
  N3: Arduino.D2, Pantalla_LCD.DB4
  N4: Arduino.D3_PWM, Pantalla_LCD.DB5
  N5: Arduino.D4, Pantalla_LCD.DB6
  N6: Arduino.D5_PWM, Pantalla_LCD.DB7
  5V: Arduino.5V, Pantalla_LCD.VDD, Pantalla_LCD.LED+, Potenciómetro.CCW
  GND: Arduino.GND, Pantalla_LCD.VSS, Pantalla_LCD.R/W, Pantalla_LCD.LED-, Potenciómetro.CW
  N7: Pantalla_LCD.V0, Potenciómetro.WIPER
