# Fritzing sketch 4-Ultrasonic (saved by Fritzing 0.9.3b)
breadboards: 1

parts:
  Arduino = Arduino Uno (Rev3)
  Pantalla_LCD = LCD screen
  Potenciómetro = TRIMPOT [package=trimpot_pth_s3_lock]
  Sensor_Ultrasonido = hc-sr04

nets:
  N1: Arduino.D8, Sensor_Ultrasonido.Echo
  N2: Arduino.D9_PWM, Sensor_Ultrasonido.Trig
  N3: Arduino.D11_PWM/MOSI, Pantalla_LCD.E
  N4: Arduino.D12/MISO, Pantalla_LCD.RS
  N5: Arduino.D2, Pantalla_LCD.DB4
  N6: Arduino.D3_PWM, Pantalla_LCD.DB5
  N7: Arduino.D4, Pantalla_LCD.DB6
  N8: Arduino.D5_PWM, Pantalla_LCD.DB7
  5V: Arduino.5V, Pantalla_LCD.VDD, Pantalla_LCD.LED+, Potenciómetro.CCW, Sensor_Ultrasonido.VCC
  GND: Arduino.GND, Pantalla_LCD.VSS, Pantalla_LCD.R/W, Pantalla_LCD.LED-, Potenciómetro.CW, Sensor_Ultrasonido.GND
  N9: Pantalla_LCD.V0, Potenciómetro.WIPER
