# Fritzing sketch 5-LED_matrix (saved by Fritzing 0.9.3b)

parts:
  Matriz_LED = 8x8 LED Modul mit MAX7219 [package=THT]
  Arduino = Arduino Uno (Rev3)

nets:
  N1: Matriz_LED.VCC_Eingang, Arduino.5V
  N2: Matriz_LED.GND_Eingang, Arduino.GND
  N3: Matriz_LED.DIN_Eingang, Arduino.D12/MISO
  N4: Matriz_LED.CS_Eingang, Arduino.D10_PWM/SS
  N5: Matriz_LED.CLK_Eingang, Arduino.D11_PWM/MOSI
