# Fritzing sketch 6-Full_system (saved by Fritzing 0.9.3b)
breadboards: 1

parts:
  Arduino = Arduino Uno (Rev3)
  Pantalla_LCD = LCD screen
  Potenciómetro = TRIMPOT [package=trimpot_pth_s3_lock]
  Sensor_Temperatura = TMP36 [package=to-92-kit]
  Sensor_efecto_hall = HALL-EFFECT [package=sc70]
  Sensor_Ultrasonido = hc-sr04
  Matriz_LED = 8x8 LED Modul mit MAX7219 [package=THT]

nets:
  N1: Arduino.A0, Sensor_Temperatura.VOUT
  N2: Arduino.D8, Sensor_efecto_hall.OUT
  N3: Arduino.D9_PWM, Matriz_LED.CLK_Eingang
  N4: Arduino.D10_PWM/SS, Matriz_LED.CS_Eingang
  N5: Arduino.D11_PWM/MOSI, Matriz_LED.DIN_Eingang
  N6: Arduino.D12/MISO, Sensor_Ultrasonido.Trig
  N7: Arduino.D13/SCK, Sensor_Ultrasonido.Echo
  N8: Arduino.D2, Pantalla_LCD.DB4
  N9: Arduino.D3_PWM, Pantalla_LCD.DB5
  N10: Arduino.D4, Pantalla_LCD.DB6
  N11: Arduino.D5_PWM, Pantalla_LCD.DB7
  N12: Arduino.D6_PWM, Pantalla_LCD.RS
  N13: Arduino.D7, Pantalla_LCD.E
  VCC: Arduino.5V, Pantalla_LCD.VDD, Pantalla_LCD.LED+, Potenciómetro.CCW, Sensor_Temperatura.VCC, Sensor_efecto_hall.VCC, Sensor_Ultrasonido.VCC, Matriz_LED.VCC_Eingang
  GND: Arduino.GND, Pantalla_LCD.VSS, Pantalla_LCD.R/W, Pantalla_LCD.LED-, Potenciómetro.CW, Sensor_Temperatura.GND, Sensor_efecto_hall.GND, Sensor_Ultrasonido.GND, Matriz_LED.GND_Eingang
  N14: Pantalla_LCD.V0, Potenciómetro.WIPER
